// Logisim project mmarc-one-logic-array-v2.circ as structural Verilog: 1 circuit, main circuit main
module main (
);

  wire accum_write, alu_op, alu_src, and_1_out, bitselector_1_out, bitselector_2_out, bitselector_3_out,
       branch, branch_sel, clk1, clk2, imm_sel, in_sel, is_zero, mem_sel, not_1_out, offset_en, read_en,
       write_en, write_sel;
  wire [2:0] bit_extender_1_out;
  wire [12:0] accum13, adder_1_out, adder_2_out, alu13, bit_extender_2_out, multiplexer_1_out,
       multiplexer_2_out, multiplexer_3_out, multiplexer_4_out, multiplexer_6_out, multiplexer_7_out, PC_q,
       ram13, ram_13, ReadOutput_q;
  wire [15:0] accum16, adder_3_out, alu16, bit_extender_3_out, instr, multiplexer_5_out, multiplexer_8_out,
       multiplexer_9_out, ram16, shifter_1_out, subtractor_1_out;

  Clock clock_1 (.out(clk1));
  Clock #(.highDuration(2), .lowDuration(2)) clock_2 (.out(clk2));
  Multiplexer #(.width(13), .enable("false")) multiplexer_1 (
    .in0(adder_1_out), .in1(adder_2_out), .out(multiplexer_1_out), .sel(and_1_out));
  Multiplexer #(.width(13), .enable("false")) multiplexer_2 (
    .in0(multiplexer_1_out), .in1(ram_13), .out(multiplexer_2_out), .sel(branch_sel));
  Shifter #(.width(16), .shift("lr")) shifter_1 (.in(instr), .\dist (4'b1101), .out(shifter_1_out));
  and and_1 (and_1_out, is_zero, branch);
  Register #(.width(13)) PC (.D(multiplexer_2_out), .en(1'b1), .Q(PC_q), .clk(clk2));  // open: clr
  Bit_Extender #(.in_width(16), .out_width(3)) bit_extender_1 (.in(shifter_1_out), .out(bit_extender_1_out));
  BitSelector #(.width(3)) bitselector_1 (.in(bit_extender_1_out), .out(bitselector_1_out), .sel(2'b10));
  BitSelector #(.width(3)) bitselector_2 (.in(bit_extender_1_out), .out(bitselector_2_out), .sel(2'b01));
  BitSelector #(.width(3)) bitselector_3 (.in(bit_extender_1_out), .out(bitselector_3_out), .sel(2'b00));
  Adder #(.width(13)) adder_1 (.a(PC_q), .b(13'h1), .out(adder_1_out));  // open: cin, cout
  datapath_logic2 datapath_logic2_1 (
    .b2(bitselector_1_out), .b1(bitselector_2_out), .b0(bitselector_3_out), .branch(branch),
    .mem_sel(mem_sel), .read_en(read_en), .write_en(write_en), .accum_write(accum_write), .alu_op(alu_op),
    .alu_src(alu_src), .in_sel(in_sel), .imm_sel(imm_sel), .offset_en(offset_en), .write_sel(write_sel),
    .branch_sel(branch_sel));
  Adder #(.width(13)) adder_2 (.a(adder_1_out), .b(bit_extender_2_out), .out(adder_2_out));  // open: cin, cout
  ROM #(.addrWidth(13), .dataWidth(16)) rom_1 (.addr(PC_q), .data(instr), .sel(1'b1));
  Bit_Extender #(.in_width(16), .out_width(13)) bit_extender_2 (.in(instr), .out(bit_extender_2_out));
  assign bit_extender_3_out = {{3{bit_extender_2_out[12]}}, bit_extender_2_out};  // Bit_Extender bit_extender_3
  Multiplexer #(.width(13), .enable("false")) multiplexer_3 (
    .in0(bit_extender_2_out), .in1(alu13), .out(multiplexer_3_out), .sel(offset_en));
  Multiplexer #(.width(13), .enable("false")) multiplexer_4 (
    .in0(bit_extender_2_out), .in1(accum13), .out(multiplexer_4_out), .sel(write_sel));
  Multiplexer #(.width(16), .enable("false")) multiplexer_5 (
    .in0(bit_extender_3_out), .in1(ram16), .out(multiplexer_5_out), .sel(alu_src));
  Multiplexer #(.width(13), .enable("false")) multiplexer_6 (
    .in0(multiplexer_3_out), .in1(multiplexer_4_out), .out(multiplexer_6_out), .sel(not_1_out));
  Multiplexer #(.width(13), .enable("false")) multiplexer_7 (
    .in0(accum13), .in1(ReadOutput_q), .out(multiplexer_7_out), .sel(in_sel));
  Multiplexer #(.width(16), .enable("false")) multiplexer_8 (
    .in0(alu16), .in1(ram16), .out(multiplexer_8_out), .sel(mem_sel));
  Multiplexer #(.width(16), .enable("false")) multiplexer_9 (
    .in0(multiplexer_8_out), .in1(bit_extender_3_out), .out(multiplexer_9_out), .sel(imm_sel));
  Adder #(.width(16)) adder_3 (.a(accum16), .b(multiplexer_5_out), .out(adder_3_out));  // open: cin, cout
  Subtractor #(.width(16)) subtractor_1 (
    .a(accum16), .b(multiplexer_5_out), .out(subtractor_1_out));  // open: bin, bout
  not not_1 (not_1_out, clk1);
  Register #(.width(16)) accumulator (.D(multiplexer_9_out), .en(accum_write), .Q(accum16), .clk(clk2));  // open: clr
  Multiplexer #(.width(16), .enable("false")) multiplexer_10 (
    .in0(adder_3_out), .in1(subtractor_1_out), .out(alu16), .sel(alu_op));
  RAM #(.addrWidth(13), .dataWidth(13), .bus("separate")) ram_1 (
    .addr(multiplexer_6_out), .din(multiplexer_7_out), .data(ram13), .str(write_en), .sel(1'b1), .clk(clk1),
    .ld(read_en));  // open: clr
  Bit_Extender #(.in_width(16), .out_width(13), .\type ("sign")) bit_extender_4 (.in(alu16), .out(alu13));
  assign ram16 = {{3{ram13[12]}}, ram13};  // Bit_Extender bit_extender_5
  Register #(.width(13)) ReadOutput (.D(ram13), .en(read_en), .Q(ReadOutput_q), .clk(not_1_out));  // open: clr
  Comparator #(.width(16)) comparator_1 (.a({16{1'b0}}), .b(accum16), .eq(is_zero));  // open: gt, lt
  Bit_Extender #(.in_width(16), .out_width(13), .\type ("sign")) bit_extender_6 (.in(accum16), .out(accum13));

  // Notes on the sheet:
  //   contents of rom_1 (hex, n*v repeats v):
  //   c01f 4000 c000 4002 1b c0ff 6002 24 c000 e000 8001 4000 2001 c000 e002 8001 4002 a009 c0ff 6000 17
  //   c000 e000 e000 4001 c000 e000 9fff 4003 c000 2003 a009 c000 4001 c026 4009 c000 1fdf c000 e001 8001
  //   4001 c000 1ff6 1fff
endmodule
