// Logisim project mmarc-one-logic-array.circ as structural Verilog: 3 circuits, main circuit main
module main (
  output offset_en
);

  wire and_1_out, bitselector_1_out, bitselector_2_out, bitselector_3_out, button_1_out, clock_1_out,
       clock_2_out, comparator_1_eq, datapath_logic2_1_accum_write, datapath_logic2_1_alu_op,
       datapath_logic2_1_alu_src, datapath_logic2_1_branch, datapath_logic2_1_branch_sel,
       datapath_logic2_1_imm_sel, datapath_logic2_1_in_sel, datapath_logic2_1_mem_sel,
       datapath_logic2_1_offset_en, datapath_logic2_1_read_en, datapath_logic2_1_write_en,
       datapath_logic2_1_write_sel, not_1_out, not_2_out;
  wire [2:0] bit_extender_1_out;
  wire [3:0] bitselector_4_out, bitselector_5_out, bitselector_6_out, bitselector_7_out;
  wire [12:0] adder_1_out, adder_2_out, bit_extender_2_out, bit_extender_5_out, bit_extender_7_out,
       multiplexer_1_out, multiplexer_2_out, multiplexer_4_out, multiplexer_5_out, multiplexer_9_out,
       multiplexer_10_out, PC_q, ram_1_data, ReadOutput_q;
  wire [15:0] Accumulator_q, adder_3_out, bit_extender_3_out, bit_extender_4_out, bit_extender_6_out,
       multiplexer_3_out, multiplexer_6_out, multiplexer_7_out, multiplexer_8_out, rom_1_data, shifter_1_out,
       subtractor_1_out;

  Shifter #(.width(16), .shift("lr")) shifter_1 (.in(rom_1_data), .\dist (4'b1101), .out(shifter_1_out));
  Bit_Extender #(.in_width(16), .out_width(3)) bit_extender_1 (.in(shifter_1_out), .out(bit_extender_1_out));
  BitSelector #(.width(3)) bitselector_1 (.in(bit_extender_1_out), .out(bitselector_1_out), .sel(2'b10));
  BitSelector #(.width(3)) bitselector_2 (.in(bit_extender_1_out), .out(bitselector_2_out), .sel(2'b01));
  BitSelector #(.width(3)) bitselector_3 (.in(bit_extender_1_out), .out(bitselector_3_out), .sel(2'b00));
  Register #(.width(13)) PC (.D(multiplexer_1_out), .en(1'b1), .Q(PC_q), .clk(clock_1_out), .clr(button_1_out));
  Clock #(.highDuration(2), .lowDuration(2)) clock_1 (.out(clock_1_out));
  Button button_1 (.out(button_1_out));
  Multiplexer #(.width(13), .enable("false")) multiplexer_1 (
    .in0(multiplexer_2_out), .in1(ram_1_data), .out(multiplexer_1_out), .sel(datapath_logic2_1_branch_sel));
  Adder #(.width(13)) adder_1 (.a(13'h1), .b(PC_q), .out(adder_1_out));  // open: cin, cout
  Adder #(.width(13)) adder_2 (.a(adder_1_out), .b(bit_extender_2_out), .out(adder_2_out));  // open: cin, cout
  Multiplexer #(.width(13), .enable("false")) multiplexer_2 (
    .in0(adder_1_out), .in1(adder_2_out), .out(multiplexer_2_out), .sel(and_1_out));
  datapath_logic2 datapath_logic2_1 (
    .b2(bitselector_1_out), .b1(bitselector_2_out), .b0(bitselector_3_out),
    .branch(datapath_logic2_1_branch), .mem_sel(datapath_logic2_1_mem_sel),
    .read_en(datapath_logic2_1_read_en), .write_en(datapath_logic2_1_write_en),
    .accum_write(datapath_logic2_1_accum_write), .alu_op(datapath_logic2_1_alu_op),
    .alu_src(datapath_logic2_1_alu_src), .in_sel(datapath_logic2_1_in_sel),
    .imm_sel(datapath_logic2_1_imm_sel), .offset_en(datapath_logic2_1_offset_en),
    .write_sel(datapath_logic2_1_write_sel), .branch_sel(datapath_logic2_1_branch_sel));
  and and_1 (and_1_out, comparator_1_eq, datapath_logic2_1_branch);
  ROM #(.addrWidth(13), .dataWidth(16)) rom_1 (.addr(PC_q), .data(rom_1_data), .sel(1'b1));
  Bit_Extender #(.in_width(16), .out_width(13)) bit_extender_2 (.in(rom_1_data), .out(bit_extender_2_out));
  assign bit_extender_3_out = {{3{bit_extender_2_out[12]}}, bit_extender_2_out};  // Bit_Extender bit_extender_3
  Register #(.width(16)) Accumulator (
    .D(multiplexer_6_out), .en(datapath_logic2_1_accum_write), .Q(Accumulator_q), .clk(clock_1_out));  // open: clr
  Multiplexer #(.width(16), .enable("false")) multiplexer_3 (
    .in0(bit_extender_3_out), .in1(bit_extender_4_out), .out(multiplexer_3_out),
    .sel(datapath_logic2_1_alu_src));
  assign bit_extender_4_out = {{3{ram_1_data[12]}}, ram_1_data};  // Bit_Extender bit_extender_4
  Adder #(.width(16)) adder_3 (.a(Accumulator_q), .b(multiplexer_3_out), .out(adder_3_out));  // open: cin, cout
  Subtractor #(.width(16)) subtractor_1 (
    .a(Accumulator_q), .b(multiplexer_3_out), .out(subtractor_1_out));  // open: bin, bout
  Multiplexer #(.width(13), .enable("false")) multiplexer_4 (
    .in0(bit_extender_2_out), .in1(bit_extender_5_out), .out(multiplexer_4_out),
    .sel(datapath_logic2_1_offset_en));
  not not_1 (not_1_out, clock_2_out);
  Multiplexer #(.width(13), .enable("false")) multiplexer_5 (
    .in0(bit_extender_2_out), .in1(bit_extender_7_out), .out(multiplexer_5_out),
    .sel(datapath_logic2_1_write_sel));
  Multiplexer #(.width(16), .enable("false")) multiplexer_6 (
    .in0(multiplexer_7_out), .in1(bit_extender_3_out), .out(multiplexer_6_out),
    .sel(datapath_logic2_1_imm_sel));
  Multiplexer #(.width(16), .enable("false")) multiplexer_7 (
    .in0(multiplexer_8_out), .in1(bit_extender_6_out), .out(multiplexer_7_out),
    .sel(datapath_logic2_1_mem_sel));
  Multiplexer #(.width(16), .enable("false")) multiplexer_8 (
    .in0(adder_3_out), .in1(subtractor_1_out), .out(multiplexer_8_out), .sel(datapath_logic2_1_alu_op));
  Bit_Extender #(.in_width(16), .out_width(13), .\type ("sign")) bit_extender_5 (
    .in(multiplexer_8_out), .out(bit_extender_5_out));
  Multiplexer #(.width(13), .enable("false")) multiplexer_9 (
    .in0(multiplexer_4_out), .in1(multiplexer_5_out), .out(multiplexer_9_out), .sel(not_1_out));
  Comparator #(.width(16)) comparator_1 (.a(Accumulator_q), .b({16{1'b0}}), .eq(comparator_1_eq));  // open: gt, lt
  Multiplexer #(.width(13), .enable("false")) multiplexer_10 (
    .in0(bit_extender_7_out), .in1(ReadOutput_q), .out(multiplexer_10_out), .sel(datapath_logic2_1_in_sel));
  RAM #(.addrWidth(13), .dataWidth(13), .bus("separate")) ram_1 (
    .addr(multiplexer_9_out), .din(multiplexer_10_out), .data(ram_1_data), .str(datapath_logic2_1_write_en),
    .sel(1'b1), .clk(clock_2_out), .ld(datapath_logic2_1_read_en));  // open: clr
  assign bit_extender_6_out = {{3{ram_1_data[12]}}, ram_1_data};  // Bit_Extender bit_extender_6
  Register #(.width(13)) ReadOutput (
    .D(ram_1_data), .en(datapath_logic2_1_read_en), .Q(ReadOutput_q), .clk(not_2_out));  // open: clr
  Bit_Extender #(.in_width(16), .out_width(13), .\type ("sign")) bit_extender_7 (
    .in(Accumulator_q), .out(bit_extender_7_out));
  not not_2 (not_2_out, clock_2_out);
  Hex_Digit_Display hex_digit_display_1 (.value(bitselector_5_out));  // open: dp
  Hex_Digit_Display hex_digit_display_2 (.value(bitselector_4_out));  // open: dp
  BitSelector #(.width(16), .group(4)) bitselector_4 (.in(Accumulator_q), .out(bitselector_4_out), .sel(2'b11));
  BitSelector #(.width(16), .group(4)) bitselector_5 (.in(Accumulator_q), .out(bitselector_5_out), .sel(2'b10));
  Clock clock_2 (.out(clock_2_out));
  Hex_Digit_Display hex_digit_display_3 (.value(bitselector_6_out));  // open: dp
  BitSelector #(.width(16), .group(4)) bitselector_6 (.in(Accumulator_q), .out(bitselector_6_out), .sel(2'b01));
  Hex_Digit_Display hex_digit_display_4 (.value(bitselector_7_out));  // open: dp
  BitSelector #(.width(16), .group(4)) bitselector_7 (.in(Accumulator_q), .out(bitselector_7_out), .sel(2'b00));

  // Notes on the sheet:
  //   b2
  //   b1
  //   b0
  //   Instruction Memory
  //   contents of rom_1 (hex, n*v repeats v):
  //   c01f 4000 c000 4002 1b c0ff 6002 24 c000 e000 8001 4000 2001 c000 e002 8001 4002 a009 c0ff 6000 17
  //   c000 e000 e000 4001 c000 e000 9fff 4003 c000 2003 a009 c000 4001 c026 4009 c000 1fdf c000 e001 8001
  //   4001 c000 1ff6 1fff
  //   Branch
  //   mem sel
  //   read en
  //   write en
  //   accum write
  //   alu op
  //   alu src
  //   in sel
  //   imm sel
  //   offset en
  //   write sel
  //   Write en
  //   mem sel
  //   alu sel
  //   imm sel
  //   offset en
  //   write sel
  //   alu op
  //   0 - read, 1 -write
  //   zero
  //   in sel
endmodule

module datapath_logic (
  input  b2,
  input  b1,
  input  b0,
  output branch,
  output mem_sel,
  output read_en,
  output write_en,
  output accum_write,
  output alu_op,
  output alu_src,
  output in_sel,
  output imm_sel,
  output offset_en,
  output write_sel
);

  wire and_3_out, and_4_out, and_5_out, and_6_out, not_1_out;

  not not_1 (not_1_out, b0);
  not not_2 (in_sel, b1);
  not not_3 (alu_op, b2);
  and and_1 (branch, alu_op, in_sel, not_1_out);
  and and_2 (mem_sel, b2, b1);
  and and_3 (and_3_out, alu_op, in_sel, b0);
  and and_4 (and_4_out, alu_op, b1, not_1_out);
  and and_5 (and_5_out, b1, b0);
  and and_6 (and_6_out, b0, in_sel);
  and and_7 (imm_sel, not_1_out, b1);
  and and_8 (offset_en, b2, b1);
  or or_1 (write_en, and_3_out, and_4_out);
  or or_2 (accum_write, and_5_out, b2);
  or or_3 (alu_src, and_6_out, alu_op);

  assign read_en = b0;
  assign write_sel = in_sel;
endmodule

module datapath_logic2 (
  input  b2,
  input  b1,
  input  b0,
  output branch,
  output mem_sel,
  output read_en,
  output write_en,
  output accum_write,
  output alu_op,
  output alu_src,
  output in_sel,
  output imm_sel,
  output offset_en,
  output write_sel,
  output branch_sel
);

  wire and_4_out, and_5_out, and_6_out, and_7_out, not_1_out, not_2_out, not_3_out, not_4_out, not_5_out,
       not_6_out, not_7_out, not_8_out, not_12_out, not_14_out;

  not not_1 (not_1_out, b2);
  not not_2 (not_2_out, b1);
  not not_3 (not_3_out, b0);
  and and_1 (mem_sel, b2, b1);
  not not_4 (not_4_out, b2);
  not not_5 (not_5_out, b1);
  not not_6 (not_6_out, b2);
  not not_7 (not_7_out, b0);
  not not_8 (not_8_out, b0);
  not not_9 (alu_op, b2);
  not not_10 (alu_src, b2);
  not not_11 (in_sel, b1);
  not not_12 (not_12_out, b0);
  and and_2 (offset_en, b2, b1);
  not not_13 (write_sel, b1);
  not not_14 (not_14_out, b1);
  and and_3 (branch, not_1_out, not_2_out, not_3_out);
  and and_4 (and_4_out, not_4_out, not_5_out, b0);
  and and_5 (and_5_out, not_6_out, b1, not_7_out);
  and and_6 (and_6_out, b1, b0);
  and and_7 (and_7_out, b2, not_8_out);
  and and_8 (imm_sel, b1, not_12_out);
  and and_9 (branch_sel, b2, not_14_out, b0);
  or or_1 (write_en, and_4_out, and_5_out);
  or or_2 (accum_write, and_6_out, and_7_out);

  assign read_en = b0;
endmodule
